// Logisim project P_Encoder.circ as structural Verilog: 1 circuit, main circuit main
module main (
  input  x0,
  input  x1,
  input  x2,
  input  x3,
  input  x4,
  input  x5,
  input  x6,
  input  x7,
  output out_9,
  output out_10,
  output out_11
);

  Priority_Encoder priority_encoder_1 (
    .in0(x0), .in1(x1), .in2(x2), .in3(x3), .in4(x4), .in5(x5), .in6(x6), .in7(x7),
    .out({out_11, out_10, out_9}));  // open: en_in, gs, en_out
endmodule
