// Logisim project ProvaMultiplexer.circ as structural Verilog: 1 circuit, main circuit main
module main (
  input  x0,
  input  x1,
  input  c,
  input  a0,
  input  a1,
  input  a2,
  input  a3,
  input  [1:0] in_8,
  output out_9,
  output out_10
);

  Multiplexer multiplexer_1 (.in0(x0), .in1(x1), .out(out_9), .sel(c));
  Multiplexer #(.select(2)) multiplexer_2 (.in0(a0), .in1(a1), .in2(a2), .in3(a3), .out(out_10), .sel(in_8));
endmodule
