// Logisim project simpleCpu.circ as structural Verilog: 3 circuits, main circuit main1
module ALU (
  input  [7:0] X,
  input  Operation,
  input  [7:0] Y,
  output [7:0] RES
);

  wire [7:0] xor_1_out;

  xor xor_1 (xor_1_out[0], Y[0], Operation);
  xor xor_2 (xor_1_out[1], Y[1], Operation);
  xor xor_3 (xor_1_out[2], Y[2], Operation);
  xor xor_4 (xor_1_out[3], Y[3], Operation);
  xor xor_5 (xor_1_out[4], Y[4], Operation);
  xor xor_6 (xor_1_out[5], Y[5], Operation);
  xor xor_7 (xor_1_out[6], Y[6], Operation);
  xor xor_8 (xor_1_out[7], Y[7], Operation);
  Adder adder_1 (.a(X), .b(xor_1_out), .out(RES), .cin(Operation));  // open: cout
endmodule

module main1 (
  input  WriteEnable,
  input  Clear,
  output [7:0] out_3
);

  wire clock_1_out, decoder_1_out0, decoder_1_out1, decoder_1_out2, decoder_1_out3, OP, SELCONST;
  wire [1:0] rom_1_data, SELDEST, SELX;
  wire [2:0] contatore3bit_1_b0;
  wire [7:0] CONST, multiplexer_1_out, multiplexer_2_out, multiplexer_3_out, R0_q, R1_q, R2_q, R3_q;

  Decoder #(.select(2)) decoder_1 (
    .out0(decoder_1_out0), .out1(decoder_1_out1), .out2(decoder_1_out2), .out3(decoder_1_out3),
    .sel(SELDEST), .en(WriteEnable));
  Clock clock_1 (.out(clock_1_out));
  Multiplexer #(.width(8)) multiplexer_1 (.in0(out_3), .in1(CONST), .out(multiplexer_1_out), .sel(SELCONST));
  Register R0 (.D(multiplexer_1_out), .en(decoder_1_out0), .clk(clock_1_out), .Q(R0_q), .clr(Clear));
  Register R1 (.D(multiplexer_1_out), .en(decoder_1_out1), .clk(clock_1_out), .Q(R1_q), .clr(Clear));
  Register R2 (.D(multiplexer_1_out), .en(decoder_1_out2), .clk(clock_1_out), .Q(R2_q), .clr(Clear));
  Register R3 (.D(multiplexer_1_out), .en(decoder_1_out3), .clk(clock_1_out), .Q(R3_q), .clr(Clear));
  Multiplexer #(.select(2), .width(8)) multiplexer_2 (
    .in0(R0_q), .in1(R1_q), .in2(R2_q), .in3(R3_q), .out(multiplexer_2_out), .sel(SELX));
  Multiplexer #(.select(2), .width(8)) multiplexer_3 (
    .in0(R0_q), .in1(R1_q), .in2(R2_q), .in3(R3_q), .out(multiplexer_3_out), .sel(rom_1_data));
  Contatore3Bit contatore3bit_1 (
    .Clock(clock_1_out), .Clear(Clear), .b2(contatore3bit_1_b0[2]), .b1(contatore3bit_1_b0[1]),
    .b0(contatore3bit_1_b0[0]));
  ROM #(.addrWidth(3), .dataWidth(16)) rom_1 (
    .addr(contatore3bit_1_b0), .data({OP, rom_1_data, SELX, SELDEST, SELCONST, CONST}));
  ALU alu_1 (.X(multiplexer_2_out), .Operation(OP), .Y(multiplexer_3_out), .RES(out_3));

  // Notes on the sheet:
  //   contents of rom_1 (hex, n*v repeats v):
  //   107 30e 2400 5600 b800
endmodule

module Contatore3Bit (
  input  Clock,
  input  Clear,
  output b2,
  output b1,
  output b0
);

  T_Flip_Flop #(.trigger("falling")) t_ff_1 (.T(1'b1), .clk(Clock), .Q(b0), .reset(Clear));  // open: Qn, preset
  T_Flip_Flop #(.trigger("falling")) t_ff_2 (.T(1'b1), .clk(b0), .Q(b1), .reset(Clear));  // open: Qn, preset
  T_Flip_Flop #(.trigger("falling")) t_ff_3 (.T(1'b1), .clk(b1), .Q(b2), .reset(Clear));  // open: Qn, preset
endmodule
